// Logisim project Controller.circ as structural Verilog: 10 circuits, main circuit Controller
module Controller (
  input  [15:0] Inst,
  input  [3:0] Flags,
  input  Clk,
  input  Reset,
  output Carry,
  output DP_Shift,
  output Imm32_Enable,
  output [4:0] Imm5,
  output [31:0] Imm32,
  output [3:0] ALU_Opcode,
  output [2:0] Rm,
  output [2:0] Rn,
  output [2:0] Rd,
  output [31:0] RAM_Addr,
  output Load,
  output Store,
  output [7:0] PC
);

  wire Conditional_1_verified, Load_Store_1_pc_hold, not_1_out, Opcode_Decoder_1_conditional,
       Opcode_Decoder_1_data_processing, Opcode_Decoder_1_load_store, Opcode_Decoder_1_shift,
       Opcode_Decoder_1_sp_address, Shift_Add_Sub_Mov_1_p3, SP_Address_1_write_enable;
  wire [2:0] Data_Processing_1_rd, Data_Processing_1_rm, Data_Processing_1_rn, Load_Store_1_rd,
       Load_Store_1_rm, Shift_Add_Sub_Mov_1_p8, Shift_Add_Sub_Mov_1_p9, Shift_Add_Sub_Mov_1_p10;
  wire [3:0] Data_Processing_1_alu_opcode, Data_Processing_1_flags_update_mask, flags_apsr_1_flags_out,
       or_1_out, Shift_Add_Sub_Mov_1_p7, Shift_Add_Sub_Mov_1_p11;
  wire [7:0] adder_1_out, adder_2_out, Conditional_1_offset;
  wire [31:0] SP_Address_1_new_stack_pointer, Stack_Pointer_q;

  Register #(.width(32)) Stack_Pointer (
    .D(SP_Address_1_new_stack_pointer), .en(SP_Address_1_write_enable), .clk(Clk), .Q(Stack_Pointer_q),
    .clr(Reset));
  Opcode_Decoder Opcode_Decoder_1 (
    .Opcode(Inst[15:10]), .Data_Processing(Opcode_Decoder_1_data_processing),
    .SP_Address(Opcode_Decoder_1_sp_address), .Load_Store(Opcode_Decoder_1_load_store),
    .Conditional(Opcode_Decoder_1_conditional), .Shift(Opcode_Decoder_1_shift));
  assign or_1_out = Data_Processing_1_flags_update_mask | Shift_Add_Sub_Mov_1_p11;  // OR_Gate or_1, 4 bits wide
  // Shift_Add_Sub_Mov Shift_Add_Sub_Mov_1: pin names not known; wires that end beside it: Inst, Opcode_Decoder_1_data_processing, Shift_Add_Sub_Mov_1_p3, Imm32_Enable, Imm5, Imm32, Shift_Add_Sub_Mov_1_p7, Shift_Add_Sub_Mov_1_p8, Shift_Add_Sub_Mov_1_p9, Shift_Add_Sub_Mov_1_p10, Shift_Add_Sub_Mov_1_p11
  Data_Processing Data_Processing_1 (
    .Instruction(Inst), .ALU_Opcode(Data_Processing_1_alu_opcode), .Enable(Opcode_Decoder_1_sp_address),
    .Rm(Data_Processing_1_rm), .Rn(Data_Processing_1_rn), .Rd(Data_Processing_1_rd),
    .Flags_Update_Mask(Data_Processing_1_flags_update_mask));
  Flags_APSR flags_apsr_1 (
    .Flags_In(or_1_out), .Update_Mask(Flags), .Clk(Clk), .Rst(Reset), .Flags_Out(flags_apsr_1_flags_out));
  Load_Store Load_Store_1 (
    .Store(Store), .Rm(Load_Store_1_rm), .Stack_Pointer(Stack_Pointer_q), .Instruction(Inst),
    .RAM_Addr(RAM_Addr), .Rd(Load_Store_1_rd), .Enable(Opcode_Decoder_1_load_store), .Load(Load), .Clk(Clk),
    .Reset(Reset), .PC_Hold(Load_Store_1_pc_hold));
  Conditional Conditional_1 (
    .Offset(Conditional_1_offset), .Instruction(Inst), .Enable(Opcode_Decoder_1_shift),
    .Verified(Conditional_1_verified), .Z(flags_apsr_1_flags_out[2]), .V(flags_apsr_1_flags_out[0]),
    .N(flags_apsr_1_flags_out[3]), .C(flags_apsr_1_flags_out[1]));
  SP_Address SP_Address_1 (
    .New_Stack_Pointer(SP_Address_1_new_stack_pointer), .Write_Enable(SP_Address_1_write_enable),
    .Stack_Pointer(Stack_Pointer_q), .Instruction(Inst), .Enable(Opcode_Decoder_1_conditional));
  Adder adder_1 (.a(8'h3), .b(Conditional_1_offset), .out(adder_1_out), .cin(1'b0));  // open: cout
  Adder adder_2 (.a(adder_1_out), .b(PC), .out(adder_2_out), .cin(1'b0));  // open: cout
  and and_1 (DP_Shift, Opcode_Decoder_1_data_processing, ~Opcode_Decoder_1_sp_address);  // AND_Gate
  not not_1 (not_1_out, Load_Store_1_pc_hold);
  Counter counter_1 (
    .clr(Reset), .load(Conditional_1_verified), .up(1'b1), .count(not_1_out), .clk(Clk), .D(adder_2_out),
    .Q(PC));  // open: carry
  Multiplexer #(.enable("false")) multiplexer_1 (
    .in0(flags_apsr_1_flags_out[1]), .in1(Shift_Add_Sub_Mov_1_p3), .out(Carry), .sel(DP_Shift));
  assign ALU_Opcode = Shift_Add_Sub_Mov_1_p7 | Data_Processing_1_alu_opcode;  // OR_Gate or_2, 4 bits wide
  assign Rm = Shift_Add_Sub_Mov_1_p8 | Data_Processing_1_rm | Load_Store_1_rm;  // OR_Gate or_3, 3 bits wide
  assign Rn = Shift_Add_Sub_Mov_1_p9 | Data_Processing_1_rn;  // OR_Gate or_4, 3 bits wide
  assign Rd = Shift_Add_Sub_Mov_1_p10 | Data_Processing_1_rd | Load_Store_1_rd;  // OR_Gate or_5, 3 bits wide

  // Notes on the sheet:
  //   Extract carry
  //   Extract Opcode
  //   IF Reg_Imm=1 THEN use shift value from register ELSE use shift value from Imm5
  //   Buffer flags for next instruction
  //   Add 3 to offset because ARM pre-increments PC
  //   and does an additionnal prefect operation
endmodule

module Conditional (
  input  Enable,
  input  [15:0] Instruction,
  input  N,
  input  Z,
  input  C,
  input  V,
  output [7:0] Offset,
  output Verified
);
endmodule

module Opcode_Decoder (
  input  [5:0] Opcode,
  output Data_Processing,
  output SP_Address,
  output Load_Store,
  output Conditional,
  output Shift
);

  wire nb0, nb1, nb2, nb3, nb4, nb5;

  not not_1 (nb0, Opcode[0]);
  not not_2 (nb1, Opcode[1]);
  not not_3 (nb2, Opcode[2]);
  not not_4 (nb3, Opcode[3]);
  not not_5 (nb4, Opcode[4]);
  not not_6 (nb5, Opcode[5]);
  and and_1 (Data_Processing, nb5, Opcode[4], nb3, nb2, nb1, nb0);
  and and_2 (SP_Address, Opcode[5], nb4, Opcode[3], nb2, Opcode[1]);
  and and_3 (Load_Store, nb5, Opcode[4], nb3, Opcode[2]);
  and and_4 (Conditional, Opcode[5], Opcode[4], nb3, Opcode[2]);
  and and_5 (Shift, nb5, nb4);

  // Other names for the same wires on the sheet: b0 = Opcode[0]; b1 = Opcode[1]; b2 = Opcode[2]; b3 = Opcode[3];
  //   b4 = Opcode[4]; b5 = Opcode[5]

  // Notes on the sheet:
  //   SP Address
  //   Load/Store
  //   Conditional branch
  //   Shift, add, sub, mov
  //   Data Processing
endmodule

module Data_Processing (
  input  [15:0] Instruction,
  input  Enable,
  output [2:0] Rn,
  output [2:0] Rd,
  output [2:0] Rm,
  output [3:0] ALU_Opcode,
  output [3:0] Flags_Update_Mask
);


  // Notes on the sheet:
  //   Note 2: RSB instruction has Rn as 1st operand.
  //   MUL instruction has Rn as 1st operand and Rdm as 2nd operand
  //   Pull output low on Enable = 0
  //   For simplification purposes, Rm is used for 1st operand both here and in the ALU.
  //   Note: instructions that does not save the result will still have the second operand as the destination register, the ALU will copy the second register to the destination register
endmodule

module Shift_Add_Sub_Mov (
  input  [15:0] Instruction,
  input  Enable,
  output [3:0] Flags_Update_Mask,
  output [4:0] Imm5,
  output [2:0] Rm,
  output [2:0] Rd,
  output Imm32_Enable,
  output [31:0] Imm32,
  output [3:0] ALU_Opcode,
  output Carry
);

  wire ADD, ADD_IMM, ASR, i0, i1, i2, i3, i4, i5, i6, i7, i8, i9, i10, LSL, LSR, MOV, not_1_out, or_1_out,
       or_2_out, or_3_out, SUB, SUB_IMM;
  wire [1:0] or_4_out;
  wire [2:0] multiplexer_5_out;
  wire [7:0] multiplexer_6_out;
  wire [15:11] inst;
  wire [31:0] bit_extender_1_out, bit_extender_2_out;

  Multiplexer #(.width(16), .enable("false")) multiplexer_1 (
    .in0({16{1'b0}}), .in1(Instruction), .out({inst, i10, i9, i8, i7, i6, i5, i4, i3, i2, i1, i0}),
    .sel(Enable));
  Opcode_Instruction opcode_instruction_1 (
    .op0(i9), .b0(ALU_Opcode[0]), .op1(i10), .b1(ALU_Opcode[1]), .op2(inst[11]), .b2(ALU_Opcode[2]),
    .op3(inst[12]), .b3(ALU_Opcode[3]));
  Decode_Operand decode_operand_1 (
    .SUB(SUB), .ADD(ADD), .ASR(ASR), .LSR(LSR), .LSL(LSL), .op4(inst[13]), .op3(inst[12]), .op2(inst[11]),
    .op1(i10), .op0(i9), .ADD_IMM(ADD_IMM), .SUB_IMM(SUB_IMM), .MOV(MOV));
  // Probe on {i0, i1, i2, i3, i4, i5, i6, i7}
  or or_1 (or_1_out, LSL, LSR, ASR);
  or or_2 (or_2_out, ADD, SUB);
  not not_1 (not_1_out, MOV);
  or or_3 (or_3_out, ADD_IMM, SUB_IMM);
  or or_4 (or_4_out[0], ADD, ADD_IMM);
  or or_5 (or_4_out[1], SUB, SUB_IMM);
  Multiplexer #(.width(5), .enable("false")) multiplexer_2 (
    .in0({5{1'b0}}), .in1({i10, i9, i8, i7, i6}), .out(Imm5), .sel(or_1_out));
  Multiplexer #(.width(3), .enable("false")) multiplexer_3 (.in0(3'b000), .in1({i8, i7, i6}), .out(Rm), .sel(or_2_out));
  Multiplexer #(.width(3), .enable("false")) multiplexer_4 (
    .in0(3'b000), .in1({i2, i1, i0}), .out(Rd), .sel(not_1_out));
  Multiplexer #(.width(3), .enable("false")) multiplexer_5 (
    .in0(3'b000), .in1({i8, i7, i6}), .out(multiplexer_5_out), .sel(or_3_out));
  or or_6 (Imm32_Enable, or_3_out, MOV);
  Multiplexer #(.width(8), .enable("false")) multiplexer_6 (
    .in0({8{1'b0}}), .in1({i0, i1, i2, i3, i4, i5, i6, i7}), .out(multiplexer_6_out), .sel(MOV));
  Multiplexer #(.select(2), .enable("false")) multiplexer_7 (
    .in0(1'b0), .in1(1'b0), .in2(1'b1), .in3(1'b0), .out(Carry), .sel(or_4_out));
  // Probe on or_4_out
  assign bit_extender_1_out = {{29{1'b0}}, multiplexer_5_out};  // Bit_Extender bit_extender_1
  assign bit_extender_2_out = {{24{1'b0}}, multiplexer_6_out};  // Bit_Extender bit_extender_2
  assign Imm32 = bit_extender_1_out | bit_extender_2_out;  // OR_Gate or_7, 32 bits wide

  // Other names for the same wires on the sheet: Imm3[2:0] = {i8, i7, i6}; Imm5_t[4:0] = {i10, i9, i8, i7, i6};
  //   Imm8[7:0] = {i0, i1, i2, i3, i4, i5, i6, i7}; inst[10:0] = {i10, i9, i8, i7, i6, i5, i4, i3, i2, i1, i0};
  //   Rm_t[2:0] = {i8, i7, i6}; Rn[2:0] = {i5, i4, i3}; Rd_t[2:0] = {i2, i1, i0}; Rdm[2:0] = {i10, i9, i8}

  // Notes on the sheet:
  //   Pull output low on Enable = 0
  //   Note 3: Imm32_Enable forces the use of the immediate for Rm register
  //   Note: ALU uses Rn register for shifts. Use Rn instead of Rm for shifts (immediate) here too
  //   Note 2: MOV uses RSB ALU opcode with Imm8 reversed so that it is copied to output register
  //   Enable carry for SUB since it is reversed in ALU
  //   ALU will use Imm32 instead of Rm
endmodule

module Load_Store (
  input  [15:0] Instruction,
  input  Enable,
  input  [31:0] Stack_Pointer,
  input  Clk,
  input  Reset,
  output Store,
  output Load,
  output PC_Hold,
  output [2:0] Rm,
  output [2:0] Rd,
  output [31:0] RAM_Addr
);


  // Notes on the sheet:
  //   Delay load and hold PC for 1 cycle for the RAM to send out requested data 
endmodule

module SP_Address (
  input  Enable,
  input  [15:0] Instruction,
  input  [31:0] Stack_Pointer,
  output Write_Enable,
  output [31:0] New_Stack_Pointer
);


  // Notes on the sheet:
  //   Pull output low on Enable = 0
endmodule

module Flags_APSR (
  input  [3:0] Flags_In,
  input  [3:0] Update_Mask,
  input  Clk,
  input  Rst,
  output [3:0] Flags_Out
);
endmodule

module Decode_Operand (
  input  op0,
  input  op1,
  input  op2,
  input  op3,
  input  op4,
  output LSL,
  output LSR,
  output ASR,
  output ADD,
  output SUB,
  output ADD_IMM,
  output SUB_IMM,
  output MOV
);

  wire not_1_out, not_2_out, not_3_out, not_4_out, not_5_out, not_6_out, not_7_out, not_8_out, not_9_out,
       not_10_out, not_11_out, not_12_out, not_13_out, not_14_out, not_15_out, not_16_out, not_17_out;

  not not_1 (not_1_out, op2);
  not not_2 (not_2_out, op3);
  not not_3 (not_3_out, op4);
  not not_4 (not_4_out, op3);
  not not_5 (not_5_out, op4);
  not not_6 (not_6_out, op2);
  not not_7 (not_7_out, op4);
  not not_8 (not_8_out, op0);
  not not_9 (not_9_out, op1);
  not not_10 (not_10_out, op4);
  not not_11 (not_11_out, op1);
  not not_12 (not_12_out, op4);
  not not_13 (not_13_out, op0);
  not not_14 (not_14_out, op4);
  not not_15 (not_15_out, op4);
  not not_16 (not_16_out, op2);
  not not_17 (not_17_out, op3);
  and and_1 (LSL, not_1_out, not_2_out, not_3_out);
  and and_2 (LSR, op2, not_4_out, not_5_out);
  and and_3 (ASR, not_6_out, op3, not_7_out);
  and and_4 (ADD, not_8_out, not_9_out, op2, op3, not_10_out);
  and and_5 (SUB, op0, not_11_out, op2, op3, not_12_out);
  and and_6 (ADD_IMM, not_13_out, op1, op2, op3, not_14_out);
  and and_7 (SUB_IMM, op0, op1, op2, op3, not_15_out);
  and and_8 (MOV, not_16_out, not_17_out, op4);
endmodule

module Opcode_Instruction (
  input  op0,
  input  op1,
  input  op2,
  input  op3,
  output b0,
  output b1,
  output b2,
  output b3
);

  wire and_1_out, and_2_out, and_3_out, not_1_out, not_2_out, not_3_out;

  not not_1 (not_1_out, op3);
  and and_1 (and_1_out, op0, op2);
  not not_2 (not_2_out, op0);
  and and_2 (and_2_out, not_2_out, op2);
  and and_3 (and_3_out, op2, not_3_out);
  not not_3 (not_3_out, op3);
  or or_1 (b2, not_1_out, and_1_out);
  or or_2 (b3, and_2_out, and_3_out);

  assign b0 = 1'b0;
  assign b1 = op3;
endmodule
